# Fritzing sketch Schematik (saved by Fritzing 0.9.3b)
breadboards: 1

parts:
  Bauteil1 = Arduino Uno (Rev3)
  LED1 = LED - 5mm [color="Red (633nm)" package="5 mm [THT]"]
  LED2 = LED - 5mm [color="Red (633nm)" package="5 mm [THT]"]
  LED4 = LED - 5mm [color="Red (633nm)" package="5 mm [THT]"]
  LED5 = LED - 5mm [color="Red (633nm)" package="5 mm [THT]"]
  LED6 = LED - 5mm [color="Red (633nm)" package="5 mm [THT]"]
  LED7 = LED - 5mm [color="Red (633nm)" package="5 mm [THT]"]
  R1 = Resistor [tolerance=±5% resistance=330 package=THT]
  R3 = Resistor [tolerance=±5% resistance=330 package=THT]
  R4 = Resistor [tolerance=±5% resistance=330 package=THT]
  R5 = Resistor [tolerance=±5% resistance=330 package=THT]
  R8 = Resistor [tolerance=±5% resistance=330 package=THT]
  R9 = Resistor [tolerance=±5% resistance=330 package=THT]
  S1 = Pushbutton [package="[THT]"]
  LED3 = LED - 5mm [color="Red (633nm)" package="5 mm [THT]"]
  R10 = Resistor [tolerance=±5% resistance=330 package=THT]

nets:
  N1: Bauteil1.D8, LED2.cathode
  N2: Bauteil1.D9_PWM, LED5.cathode
  N3: Bauteil1.D10_PWM/SS, LED3.cathode
  N4: Bauteil1.D11_PWM/MOSI, LED1.cathode
  N5: Bauteil1.D2, Bauteil1.GND, R1.Pin_0, R3.Pin_0, S1.Pin_1, S1.Pin_2
  N6: Bauteil1.D5_PWM, LED4.anode
  N7: Bauteil1.D6_PWM, LED6.anode
  N8: Bauteil1.D7, LED7.cathode
  N9: Bauteil1.5V, S1.Pin_3, S1.Pin_4, R10.Pin_0
  N10: LED1.anode, R4.Pin_0
  N11: LED2.anode, R9.Pin_0
  N12: LED5.anode, R3.Pin_1
  N13: LED6.cathode, R5.Pin_0
  N14: LED7.anode, R10.Pin_1
  N15: R1.Pin_1, R5.Pin_1, R9.Pin_1
  N16: R8.Pin_0, LED3.anode
